// Logisim project ALU_24_bit.circ as structural Verilog: 2 circuits, main circuit ALU
module ALU (
  input  [2:0] in_1,
  input  [23:0] in_2,
  input  [23:0] in_3,
  input  [4:0] in_4,
  output [23:0] out_5,
  output out_6
);

  ALU_24_bit alu_24_bit_1 (.S(in_1), .shmt(in_4), .A(in_2), .B(in_3), .Zero(out_6), .Result(out_5));

  // Notes on the sheet:
  //   ALU_24_bit
endmodule

module ALU_24_bit (
  input  [23:0] A,
  input  [23:0] B,
  input  [4:0] shmt,
  input  [2:0] S,
  output [23:0] Result,
  output Zero
);

  wire comparator_1_gt, comparator_1_lt;
  wire [23:0] adder_1_out, adder_2_out, bit_extender_1_out, bit_extender_2_out, shifter_1_out, shifter_2_out,
       subtractor_1_out, xor_1_out;

  Adder #(.width(24)) adder_1 (.a(A), .b(B), .out(adder_1_out));  // open: cin, cout
  Subtractor #(.width(24)) subtractor_1 (.a(A), .b(B), .out(subtractor_1_out));  // open: bin, bout
  Adder #(.width(24)) adder_2 (.a(A), .b(24'h1), .out(adder_2_out));  // open: cin, cout
  Shifter #(.width(24)) shifter_1 (.in(A), .\dist (shmt), .out(shifter_1_out));
  Shifter #(.shift("lr"), .width(24)) shifter_2 (.in(A), .\dist (shmt), .out(shifter_2_out));
  Comparator #(.width(24)) comparator_1 (.a(A), .b(B), .gt(comparator_1_gt), .lt(comparator_1_lt));  // open: eq
  assign xor_1_out = A ^ B;  // XOR_Gate xor_1, 24 bits wide
  assign bit_extender_1_out = {{23{comparator_1_gt}}, comparator_1_gt};  // Bit_Extender bit_extender_1
  assign bit_extender_2_out = {{23{comparator_1_lt}}, comparator_1_lt};  // Bit_Extender bit_extender_2
  Multiplexer #(.select(3), .width(24)) multiplexer_1 (
    .in0(adder_1_out), .in1(subtractor_1_out), .in2(adder_2_out), .in3(shifter_1_out), .in4(shifter_2_out),
    .in5(xor_1_out), .in6(bit_extender_1_out), .in7(bit_extender_2_out), .out(Result), .sel(S));
  nor nor_1 (Zero, Result[0], Result[1], Result[2], Result[3], Result[4], Result[5], Result[6], Result[7], Result[8], Result[9], Result[10], Result[11], Result[12], Result[13], Result[14], Result[15], Result[16], Result[17], Result[18], Result[19], Result[20], Result[21], Result[22], Result[23]);
endmodule
