// Logisim project ALU_Cuntrol_unit_2.circ as structural Verilog: 2 circuits, main circuit alu_control
module alu_control (
  input  [3:0] in_1,
  output [2:0] out_2,
  output out_3,
  output out_4,
  output out_5,
  output out_6,
  output out_7,
  output out_8,
  output out_9,
  output out_10
);

  ALU_Control_unit2 alu_control_unit2_1 (
    .opcode(in_1), .op2(out_2[1]), .op1(out_2[0]), .reg_write(out_3), .reg_des(out_4), .ALU_src(out_5),
    .Mem_red(out_6), .Mem_write(out_7), .Mem_to_reg(out_8), .jump(out_9), .Branch(out_10), .op3(out_2[2]));

  // Notes on the sheet:
  //   Control_Unit
endmodule

module ALU_Control_unit2 (
  input  [3:0] opcode,
  output op3,
  output op2,
  output op1,
  output reg_write,
  output reg_des,
  output ALU_src,
  output Mem_red,
  output Mem_write,
  output Mem_to_reg,
  output jump,
  output Branch
);

  wire and_1_out, and_2_out, and_3_out, and_4_out, and_5_out, and_6_out, and_7_out, and_8_out, and_9_out,
       and_10_out, and_11_out, and_12_out, and_13_out, and_14_out, and_15_out, and_16_out, and_17_out,
       and_18_out, and_19_out, and_20_out, and_21_out, and_22_out, and_23_out, and_24_out, and_25_out,
       and_26_out, and_27_out, and_28_out, and_29_out, and_30_out, and_31_out, and_32_out, and_33_out,
       and_34_out, and_35_out, and_36_out, and_42_out, and_43_out, and_44_out, and_45_out, not_1_out,
       not_2_out, not_3_out, not_4_out, or_1_out, or_2_out, or_3_out, or_5_out, or_8_out, or_10_out,
       or_11_out;

  not not_1 (not_1_out, opcode[3]);
  not not_2 (not_2_out, opcode[2]);
  not not_3 (not_3_out, opcode[1]);
  not not_4 (not_4_out, opcode[0]);
  and and_1 (and_1_out, not_1_out, opcode[2]);
  and and_2 (and_2_out, opcode[3], opcode[1]);
  and and_3 (and_3_out, opcode[3], opcode[2]);
  and and_4 (and_4_out, opcode[2], not_3_out);
  and and_5 (and_5_out, not_1_out, opcode[1]);
  and and_6 (and_6_out, not_1_out, opcode[2]);
  and and_7 (and_7_out, not_2_out, opcode[0]);
  and and_8 (and_8_out, not_1_out, not_4_out);
  and and_9 (and_9_out, not_1_out, opcode[2]);
  and and_10 (and_10_out, not_2_out, not_3_out);
  and and_11 (and_11_out, opcode[3], opcode[1]);
  and and_12 (and_12_out, opcode[3], not_2_out);
  and and_13 (and_13_out, not_3_out, opcode[0]);
  and and_14 (and_14_out, opcode[3], opcode[1]);
  and and_15 (and_15_out, opcode[3], not_2_out);
  and and_16 (and_16_out, opcode[2], opcode[1]);
  and and_17 (and_17_out, opcode[3], not_2_out);
  and and_18 (and_18_out, not_3_out, not_4_out);
  and and_19 (and_19_out, and_1_out, opcode[0]);
  and and_20 (and_20_out, opcode[2], opcode[1]);
  and and_21 (and_21_out, and_2_out, opcode[0]);
  and and_22 (and_22_out, and_3_out, not_4_out);
  and and_23 (and_23_out, opcode[1], opcode[0]);
  and and_24 (and_24_out, and_4_out, not_4_out);
  and and_25 (and_25_out, and_5_out, not_4_out);
  and and_26 (and_26_out, and_6_out, not_4_out);
  and and_27 (and_27_out, opcode[3], not_2_out);
  and and_28 (and_28_out, not_3_out, not_4_out);
  and and_29 (and_29_out, opcode[3], opcode[1]);
  and and_30 (and_30_out, opcode[3], opcode[2]);
  or or_1 (or_1_out, and_7_out, and_8_out);
  and and_31 (and_31_out, opcode[2], not_3_out);
  and and_32 (and_32_out, not_3_out, opcode[0]);
  and and_33 (and_33_out, and_9_out, not_3_out);
  and and_34 (and_34_out, and_10_out, opcode[0]);
  and and_35 (and_35_out, and_11_out, not_4_out);
  and and_36 (and_36_out, opcode[3], not_3_out);
  and and_37 (Mem_red, and_12_out, and_13_out);
  and and_38 (Mem_write, and_14_out, not_4_out);
  and and_39 (Mem_to_reg, and_15_out, not_3_out);
  and and_40 (jump, and_16_out, opcode[0]);
  and and_41 (Branch, and_17_out, and_18_out);
  or or_2 (or_2_out, and_19_out, and_20_out);
  or or_3 (or_3_out, and_21_out, and_22_out);
  or or_4 (op2, and_23_out, and_24_out);
  or or_5 (or_5_out, and_25_out, and_26_out);
  and and_42 (and_42_out, and_27_out, and_28_out);
  and and_43 (and_43_out, and_29_out, opcode[0]);
  and and_44 (and_44_out, and_30_out, opcode[0]);
  or or_6 (reg_write, or_1_out, and_31_out);
  or or_7 (reg_des, and_32_out, and_33_out);
  or or_8 (or_8_out, and_34_out, and_35_out);
  and and_45 (and_45_out, and_36_out, opcode[0]);
  or or_9 (op3, or_2_out, or_3_out);
  or or_10 (or_10_out, or_5_out, and_42_out);
  or or_11 (or_11_out, and_43_out, and_44_out);
  or or_12 (ALU_src, or_8_out, and_45_out);
  or or_13 (op1, or_10_out, or_11_out);
endmodule
