// Logisim project Datapath_24bit.circ as structural Verilog
module DataPath (
  input  RAM_CLK,
  input  PC_REG_CLK,
  output [23:0] out_3
);

  wire alu_24_bit_1_zero, alu_control_unit2_1_alu_src, alu_control_unit2_1_branch, alu_control_unit2_1_jump,
       alu_control_unit2_1_mem_red, alu_control_unit2_1_mem_to_reg, alu_control_unit2_1_mem_write,
       alu_control_unit2_1_reg_des, alu_control_unit2_1_reg_write, and_1_out;
  wire [2:0] alu_control_unit2_1_op1;
  wire [4:0] multiplexer_3_out, rom_1_data_2, rom_1_data_3, rom_1_data_4, rom_1_data_5;
  wire [23:0] adder_1_out, adder_2_out, bit_extender_1_out, bit_extender_2_out, multiplexer_1_out,
       multiplexer_2_out, multiplexer_4_out, multiplexer_5_out, ram_1_dout, register_1_q,
       register_file_24_bit_1_read_data_1, register_file_24_bit_1_read_data_2;
  wire [23:20] rom_1_data;

  and and_1 (and_1_out, alu_24_bit_1_zero, alu_control_unit2_1_branch);
  Adder #(.width(24)) adder_1 (.a(bit_extender_2_out), .b(register_1_q), .out(adder_1_out));  // open: cin, cout
  Multiplexer #(.width(24)) multiplexer_1 (
    .in0(adder_2_out), .in1(adder_1_out), .out(multiplexer_1_out), .sel(and_1_out));
  Multiplexer #(.width(24)) multiplexer_2 (
    .in0(multiplexer_1_out), .in1(bit_extender_1_out), .out(multiplexer_2_out), .sel(alu_control_unit2_1_jump));
  Register #(.width(24)) register_1 (
    .D(multiplexer_2_out), .en(1'b1), .clk(PC_REG_CLK), .Q(register_1_q));  // open: clr
  Adder #(.width(24)) adder_2 (.a(24'h1), .b(register_1_q), .out(adder_2_out));  // open: cin, cout
  ROM #(.addrWidth(24), .dataWidth(24)) rom_1 (
    .addr(register_1_q), .data({rom_1_data, rom_1_data_3, rom_1_data_2, rom_1_data_5, rom_1_data_4}));
  assign bit_extender_1_out = {{4{rom_1_data_3[4]}}, {rom_1_data_3, rom_1_data_2, rom_1_data_5, rom_1_data_4}};  // Bit_Extender bit_extender_1
  Multiplexer #(.width(5)) multiplexer_3 (
    .in0(rom_1_data_5), .in1(rom_1_data_2), .out(multiplexer_3_out), .sel(alu_control_unit2_1_reg_des));
  Register_file_24_bit register_file_24_bit_1 (
    .Write(alu_control_unit2_1_reg_write), .Write_address(multiplexer_3_out), .CLK(PC_REG_CLK),
    .Read_address_1(rom_1_data_3), .Read_address_2(rom_1_data_2), .Write_data(multiplexer_5_out),
    .Read_data_2(register_file_24_bit_1_read_data_2), .Read_data_1(register_file_24_bit_1_read_data_1));
  ALU_Control_unit2 alu_control_unit2_1 (
    .opcode(rom_1_data), .op2(alu_control_unit2_1_op1[1]), .op1(alu_control_unit2_1_op1[0]),
    .reg_write(alu_control_unit2_1_reg_write), .reg_des(alu_control_unit2_1_reg_des),
    .ALU_src(alu_control_unit2_1_alu_src), .Mem_red(alu_control_unit2_1_mem_red),
    .Mem_write(alu_control_unit2_1_mem_write), .Mem_to_reg(alu_control_unit2_1_mem_to_reg),
    .jump(alu_control_unit2_1_jump), .Branch(alu_control_unit2_1_branch), .op3(alu_control_unit2_1_op1[2]));
  assign bit_extender_2_out = {{14{1'b0}}, {rom_1_data_5, rom_1_data_4}};  // Bit_Extender bit_extender_2
  Multiplexer #(.width(24)) multiplexer_4 (
    .in0(register_file_24_bit_1_read_data_2), .in1(bit_extender_2_out), .out(multiplexer_4_out),
    .sel(alu_control_unit2_1_alu_src));
  Multiplexer #(.width(24)) multiplexer_5 (
    .in0(out_3), .in1(ram_1_dout), .out(multiplexer_5_out), .sel(alu_control_unit2_1_mem_to_reg));
  ALU_24_bit alu_24_bit_1 (
    .S(alu_control_unit2_1_op1), .shmt(rom_1_data_4), .A(register_file_24_bit_1_read_data_1),
    .B(multiplexer_4_out), .Zero(alu_24_bit_1_zero), .Result(out_3));
  RAM #(.addrWidth(24), .dataWidth(24)) ram_1 (
    .addr(out_3), .we(alu_control_unit2_1_mem_write), .oe(alu_control_unit2_1_mem_red), .clk(RAM_CLK),
    .din(register_file_24_bit_1_read_data_2), .dout(ram_1_dout));
endmodule
