// Logisim project Registerfile_24_bit.circ as structural Verilog: 2 circuits, main circuit Register_file
module Register_file (
  input  [4:0] in_1,
  input  [4:0] in_2,
  input  [4:0] in_3,
  input  [23:0] in_4,
  input  in_5,
  input  in_6,
  output [23:0] out_7,
  output [23:0] out_8
);

  Register_file_24_bit register_file_24_bit_1 (
    .Write(in_6), .Write_address(in_3), .CLK(in_5), .Read_address_1(in_1), .Read_address_2(in_2),
    .Write_data(in_4), .Read_data_2(out_8), .Read_data_1(out_7));
endmodule

module Register_file_24_bit (
  input  [23:0] Write_data,
  input  Write,
  input  [4:0] Write_address,
  input  CLK,
  input  [4:0] Read_address_1,
  input  [4:0] Read_address_2,
  output [23:0] Read_data_1,
  output [23:0] Read_data_2
);

  wire decoder_1_out0, decoder_1_out1, decoder_1_out2, decoder_1_out3, decoder_1_out4, decoder_1_out5,
       decoder_1_out6, decoder_1_out7, decoder_1_out8, decoder_1_out9, decoder_1_out10, decoder_1_out11,
       decoder_1_out12, decoder_1_out13, decoder_1_out14, decoder_1_out15, decoder_1_out16, decoder_1_out17,
       decoder_1_out18, decoder_1_out19, decoder_1_out20, decoder_1_out21, decoder_1_out22, decoder_1_out23,
       decoder_1_out24, decoder_1_out25, decoder_1_out26, decoder_1_out27, decoder_1_out28, decoder_1_out29,
       decoder_1_out30, decoder_1_out31;
  wire [23:0] register_1_q, register_2_q, register_3_q, register_4_q, register_5_q, register_6_q,
       register_7_q, register_8_q, register_9_q, register_10_q, register_11_q, register_12_q, register_13_q,
       register_14_q, register_15_q, register_16_q, register_17_q, register_18_q, register_19_q,
       register_20_q, register_21_q, register_22_q, register_23_q, register_24_q, register_25_q,
       register_26_q, register_27_q, register_28_q, register_29_q, register_30_q, register_31_q,
       register_32_q;

  Decoder #(.select(5)) decoder_1 (
    .out0(decoder_1_out0), .out1(decoder_1_out1), .out2(decoder_1_out2), .out3(decoder_1_out3),
    .out4(decoder_1_out4), .out5(decoder_1_out5), .out6(decoder_1_out6), .out7(decoder_1_out7),
    .out8(decoder_1_out8), .out9(decoder_1_out9), .out10(decoder_1_out10), .out11(decoder_1_out11),
    .out12(decoder_1_out12), .out13(decoder_1_out13), .out14(decoder_1_out14), .out15(decoder_1_out15),
    .out16(decoder_1_out16), .out17(decoder_1_out17), .out18(decoder_1_out18), .out19(decoder_1_out19),
    .out20(decoder_1_out20), .out21(decoder_1_out21), .out22(decoder_1_out22), .out23(decoder_1_out23),
    .out24(decoder_1_out24), .out25(decoder_1_out25), .out26(decoder_1_out26), .out27(decoder_1_out27),
    .out28(decoder_1_out28), .out29(decoder_1_out29), .out30(decoder_1_out30), .out31(decoder_1_out31),
    .sel(Write_address), .en(Write));
  Register #(.width(24)) register_1 (.D(Write_data), .en(decoder_1_out0), .clk(CLK), .Q(register_1_q));  // open: clr
  Register #(.width(24)) register_2 (.D(Write_data), .en(decoder_1_out1), .clk(CLK), .Q(register_2_q));  // open: clr
  Register #(.width(24)) register_3 (.D(Write_data), .en(decoder_1_out2), .clk(CLK), .Q(register_3_q));  // open: clr
  Register #(.width(24)) register_4 (.D(Write_data), .en(decoder_1_out3), .clk(CLK), .Q(register_4_q));  // open: clr
  Register #(.width(24)) register_5 (.D(Write_data), .en(decoder_1_out4), .clk(CLK), .Q(register_5_q));  // open: clr
  Register #(.width(24)) register_6 (.D(Write_data), .en(decoder_1_out5), .clk(CLK), .Q(register_6_q));  // open: clr
  Register #(.width(24)) register_7 (.D(Write_data), .en(decoder_1_out6), .clk(CLK), .Q(register_7_q));  // open: clr
  Register #(.width(24)) register_8 (.D(Write_data), .en(decoder_1_out7), .clk(CLK), .Q(register_8_q));  // open: clr
  Register #(.width(24)) register_9 (.D(Write_data), .en(decoder_1_out8), .clk(CLK), .Q(register_9_q));  // open: clr
  Register #(.width(24)) register_10 (.D(Write_data), .en(decoder_1_out9), .clk(CLK), .Q(register_10_q));  // open: clr
  Register #(.width(24)) register_11 (.D(Write_data), .en(decoder_1_out10), .clk(CLK), .Q(register_11_q));  // open: clr
  Register #(.width(24)) register_12 (.D(Write_data), .en(decoder_1_out11), .clk(CLK), .Q(register_12_q));  // open: clr
  Register #(.width(24)) register_13 (.D(Write_data), .en(decoder_1_out12), .clk(CLK), .Q(register_13_q));  // open: clr
  Register #(.width(24)) register_14 (.D(Write_data), .en(decoder_1_out13), .clk(CLK), .Q(register_14_q));  // open: clr
  Register #(.width(24)) register_15 (.D(Write_data), .en(decoder_1_out14), .clk(CLK), .Q(register_15_q));  // open: clr
  Register #(.width(24)) register_16 (.D(Write_data), .en(decoder_1_out15), .clk(CLK), .Q(register_16_q));  // open: clr
  Register #(.width(24)) register_17 (.D(Write_data), .en(decoder_1_out16), .clk(CLK), .Q(register_17_q));  // open: clr
  Register #(.width(24)) register_18 (.D(Write_data), .en(decoder_1_out17), .clk(CLK), .Q(register_18_q));  // open: clr
  Register #(.width(24)) register_19 (.D(Write_data), .en(decoder_1_out18), .clk(CLK), .Q(register_19_q));  // open: clr
  Register #(.width(24)) register_20 (.D(Write_data), .en(decoder_1_out19), .clk(CLK), .Q(register_20_q));  // open: clr
  Register #(.width(24)) register_21 (.D(Write_data), .en(decoder_1_out20), .clk(CLK), .Q(register_21_q));  // open: clr
  Register #(.width(24)) register_22 (.D(Write_data), .en(decoder_1_out21), .clk(CLK), .Q(register_22_q));  // open: clr
  Register #(.width(24)) register_23 (.D(Write_data), .en(decoder_1_out22), .clk(CLK), .Q(register_23_q));  // open: clr
  Register #(.width(24)) register_24 (.D(Write_data), .en(decoder_1_out23), .clk(CLK), .Q(register_24_q));  // open: clr
  Register #(.width(24)) register_25 (.D(Write_data), .en(decoder_1_out24), .clk(CLK), .Q(register_25_q));  // open: clr
  Register #(.width(24)) register_26 (
    .D(Write_data), .en(decoder_1_out25), .clk(decoder_1_out24), .Q(register_26_q));  // open: clr
  Register #(.width(24)) register_27 (
    .D(Write_data), .en(decoder_1_out26), .clk(decoder_1_out24), .Q(register_27_q));  // open: clr
  Register #(.width(24)) register_28 (
    .D(Write_data), .en(decoder_1_out27), .clk(decoder_1_out24), .Q(register_28_q));  // open: clr
  Register #(.width(24)) register_29 (
    .D(Write_data), .en(decoder_1_out28), .clk(decoder_1_out24), .Q(register_29_q));  // open: clr
  Register #(.width(24)) register_30 (
    .D(Write_data), .en(decoder_1_out29), .clk(decoder_1_out24), .Q(register_30_q));  // open: clr
  Register #(.width(24)) register_31 (
    .D(Write_data), .en(decoder_1_out30), .clk(decoder_1_out24), .Q(register_31_q));  // open: clr
  Register #(.width(24)) register_32 (
    .D(Write_data), .en(decoder_1_out31), .clk(decoder_1_out24), .Q(register_32_q));  // open: clr
  Multiplexer #(.select(5), .width(24)) multiplexer_1 (
    .in0(register_1_q), .in1(register_2_q), .in2(register_3_q), .in3(register_4_q), .in4(register_5_q),
    .in5(register_6_q), .in6(register_7_q), .in7(register_8_q), .in8(register_9_q), .in9(register_10_q),
    .in10(register_11_q), .in11(register_12_q), .in12(register_13_q), .in13(register_14_q),
    .in14(register_15_q), .in15(register_16_q), .in16(register_17_q), .in17(register_18_q),
    .in18(register_19_q), .in19(register_20_q), .in20(register_21_q), .in21(register_22_q),
    .in22(register_23_q), .in23(register_24_q), .in24(register_25_q), .in25(register_26_q),
    .in26(register_27_q), .in27(register_28_q), .in28(register_29_q), .in29(register_30_q),
    .in30(register_31_q), .in31(register_32_q), .out(Read_data_1), .sel(Read_address_1));
  Multiplexer #(.select(5), .width(24)) multiplexer_2 (
    .in0(register_1_q), .in1(register_2_q), .in2(register_3_q), .in3(register_4_q), .in4(register_5_q),
    .in5(register_6_q), .in6(register_7_q), .in7(register_8_q), .in8(register_9_q), .in9(register_10_q),
    .in10(register_11_q), .in11(register_12_q), .in12(register_13_q), .in13(register_14_q),
    .in14(register_15_q), .in15(register_16_q), .in16(register_17_q), .in17(register_18_q),
    .in18(register_19_q), .in19(register_20_q), .in20(register_21_q), .in21(register_22_q),
    .in22(register_23_q), .in23(register_24_q), .in24(register_25_q), .in25(register_26_q),
    .in26(register_27_q), .in27(register_28_q), .in28(register_29_q), .in29(register_30_q),
    .in30(register_31_q), .in31(register_32_q), .out(Read_data_2), .sel(Read_address_2));
endmodule
